// Digital circuit HW1 2-Bit-Multiplier.dig as structural Verilog
module HW1_2_Bit_Multiplier (
  input  A1,
  input  A0,
  input  B1,
  input  B0,
  output P3,
  output P2,
  output P1,
  output P0
);

  wire and_2_out, and_3_out, and_4_out, half_adder_1_cout;

  and and_1 (P0, A0, B0);
  and and_2 (and_2_out, A1, B0);
  and and_3 (and_3_out, B1, A0);
  and and_4 (and_4_out, B1, A1);
  half_adder half_adder_1 (.A(and_2_out), .B(and_3_out), .Sum(P1), .Cout(half_adder_1_cout));
  half_adder half_adder_2 (.A(half_adder_1_cout), .B(and_4_out), .Sum(P2), .Cout(P3));
endmodule
