// Digital circuit HW1 4-Bit-Ripple-Carry-Adder.dig as structural Verilog
module HW1_4_Bit_Ripple_Carry_Adder (
  input  [3:0] A,
  input  [3:0] B,
  input  [3:0] Carry_In,
  output [3:0] Sum,
  output [3:0] Carry_Out
);

  _1_bit_adder _1_bit_adder_1 (.A(A[3]), .B(B[3]), .sum(Sum[3]));  // open: Carry_in, carry_out
  _1_bit_adder _1_bit_adder_2 (.A(A[2]), .B(B[2]), .sum(Sum[2]));  // open: Carry_in, carry_out
  _1_bit_adder _1_bit_adder_3 (.A(A[1]), .B(B[1]), .sum(Sum[1]));  // open: Carry_in, carry_out
  _1_bit_adder _1_bit_adder_4 (.A(A[0]), .B(B[0]), .sum(Sum[0]));  // open: Carry_in, carry_out
endmodule
