// Digital circuit HW1 4-bit Adder.dig as structural Verilog
module HW1_4_bit_Adder (
  input  [3:0] A,
  input  [3:0] B,
  output [3:0] Sum,
  output carry_out
);

  wire _1_bit_adder_2_carry_out, _1_bit_adder_3_carry_out, _1_bit_adder_4_carry_out;

  _1_bit_adder _1_bit_adder_1 (
    .A(A[3]), .B(B[3]), .Carry_in(_1_bit_adder_2_carry_out), .sum(Sum[3]), .carry_out(carry_out));
  _1_bit_adder _1_bit_adder_2 (
    .A(A[2]), .B(B[2]), .Carry_in(_1_bit_adder_3_carry_out), .sum(Sum[2]),
    .carry_out(_1_bit_adder_2_carry_out));
  _1_bit_adder _1_bit_adder_3 (
    .A(A[1]), .B(B[1]), .Carry_in(_1_bit_adder_4_carry_out), .sum(Sum[1]),
    .carry_out(_1_bit_adder_3_carry_out));
  _1_bit_adder _1_bit_adder_4 (.A(A[0]), .B(B[0]), .Carry_in(1'b0), .sum(Sum[0]), .carry_out(_1_bit_adder_4_carry_out));
endmodule
