// Digital circuit HW1 Half-Adder.dig as structural Verilog
module HW1_Half_Adder (
  input  A,
  input  B,
  output Sum,
  output Cout
);

  xor xor_1 (Sum, A, B);
  and and_1 (Cout, A, B);
endmodule
