// Digital circuit HW2 Question 1B.dig as structural Verilog
module HW2_Question_1B (
  input  A,
  input  B,
  input  C,
  output A_And_B,
  output A_And_B__Or_C
);

  and and_1 (A_And_B, A, B);
  or or_1 (A_And_B__Or_C, A_And_B, C);
endmodule
